# Fritzing sketch VR_leds (saved by Fritzing 0.9.8b)
breadboards: 1

parts:
  Mod1 = Raspberry Pi Pico
  C1 = Ceramic Capacitor [capacitance=100nF voltage=35V package="100 mil [THT, multilayer]"]
  C3 = Electrolytic Capacitor [capacitance=0.1mF voltage=35V package="100 mil [THT, electrolytic]"]
  パーツ1 = NeoPixel NeoMatrix 8x8 [part_number=1487]
  R1 = Resistor [tolerance=±5% power=0.25 resistance=2.2 package=THT]
  R2 = Rotary Potentiometer (Small) [maximum_resistance=100kΩ package=THT]
  R3 = Rotary Potentiometer (Small) [maximum_resistance=100kΩ package=THT]
  R4 = Rotary Potentiometer (Small) [maximum_resistance=100kΩ package=THT]
  VCC1 = 4 x AAA Battery Mount

nets:
  N1: Mod1.pin_3, Mod1.pin_8, Mod1.pin_13, Mod1.pin_18, Mod1.pin_28, Mod1.pin_33, Mod1.pin_38, C1.0, C1.1, C3.-, C3.+, パーツ1.GND, R2.leg1, R2.leg2, R3.leg1, R3.leg2, R4.leg1, R4.wiper, R4.leg2, VCC1.-
  N2: Mod1.pin_21, パーツ1.IN
  N3: パーツ1.VDD, R1.Pin_0
  N4: R1.Pin_1, VCC1.+

notes:
  WS2812B用
  電源3.5-5.5V
  ラズベリーパイPico
  WS2812B 10x10
  VR0,VR1,VR2

custom parts:
  Raspberry Pi Pico: Raspberry Pi Pico. Based around the RP2040 microcontroller the Pico is a low cost microcontroller device bringing Raspberry Pi quality, cost, and easy of use to the microcontroller space. Jan 2021, Split part in to two versions: tht (this one) and SMD. This one will drill holes for a .1 in header in pcb to allow plugging in the module as well as providing pads to solder the module to the top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
  NeoPixel NeoMatrix 8x8: Put on your sunglasses before wiring up this LED matrix - 64 eye-blistering RGB LEDs adorn the NeoMatrix for a blast of configurable color. Arranged in an 8x8 matrix, each pixel is individually addressable. Only one microcontroller pin is required to control all the LEDs, and you get 24 bit color for each LED.
